# Fritzing sketch dioramaEffects (saved by Fritzing 0.9.3b)
breadboards: 1

parts:
  Arduino = Arduino Pro Mini v13
  1N4001_DIODE_PUMP = Diode [package=diode-1n4148]
  R1_220_RED = Resistor [tolerance=±5% resistance=220 package="0603 [SMD]"]
  R2_220_GREEN = Resistor [tolerance=±5% resistance=220 package="0603 [SMD]"]
  R3_220_BLUE = Resistor [tolerance=±5% resistance=220 package="0603 [SMD]"]
  U1 = Voltage Regulator [package=to220-adj]  # not connected
  R_1K_ACTIVATOR_BUTTON = Resistor [tolerance=±5% resistance=1k package="1206 [SMD]"]  # not connected
  LIGHT_EFFECT_SWITCH = Toggle Switch [package=THT]  # not connected
  TIMER_SWITCH = Toggle Switch [package=THT]  # not connected
  ACTIVATOR_BUTTON = Momentary Switch [package=ksa_sealed_tac_switch]  # not connected
  PIR_SENSOR = PIR sensor  # not connected
  PN2222_TRANSISTOR_PUMP = TRANSISTOR_PNP [package=to-92]
  R5_330_PUMP = Resistor [tolerance=±5% resistance=330 package="0603 [SMD]"]
  LED1 = RGB LED - (4 legs) [package="5 mm [THT]"]
  R_1K_LIGHT_EFFECT_SWITCH = Resistor [tolerance=±5% resistance=1k package="1206 [SMD]"]  # not connected
  R_1K_TIMER_SWITCH = Resistor [tolerance=±5% resistance=1k package="1206 [SMD]"]  # not connected

nets:
  N1: Arduino.GND, PN2222_TRANSISTOR_PUMP.E, LED1.common_anode
  N2: Arduino.D9_PWM, R5_330_PUMP.Pin_0
  N3: Arduino.D8, R1_220_RED.Pin_1
  N4: Arduino.D7, R2_220_GREEN.Pin_1
  N5: Arduino.D6_PWM, R3_220_BLUE.Pin_1
  N6: 1N4001_DIODE_PUMP.A, PN2222_TRANSISTOR_PUMP.C
  N7: R1_220_RED.Pin_0, LED1.red_cathode
  N8: R2_220_GREEN.Pin_0, LED1.green_cathode
  N9: R3_220_BLUE.Pin_0, LED1.blue_cathode
  N10: PN2222_TRANSISTOR_PUMP.B, R5_330_PUMP.Pin_1
